// Logisim project 1-5.circ as structural Verilog: 2 circuits, main circuit main
module main (
  input  C0,
  input  A0,
  input  B0,
  input  A1,
  input  B1,
  input  A2,
  input  B2,
  input  A3,
  input  B3,
  output S0,
  output S1,
  output S2,
  output S3,
  output C4
);

  wire and_1_out, and_2_out, and_3_out, and_4_out, and_5_out, and_6_out, and_7_out, and_8_out, and_9_out,
       and_10_out, and_11_out, and_12_out, and_13_out, and_14_out, or_1_out, or_2_out, or_3_out, xor_1_out,
       xor_2_out, xor_3_out, xor_4_out;

  xor xor_1 (xor_1_out, A0, B0);
  and and_1 (and_1_out, A0, B0);
  xor xor_2 (xor_2_out, A1, B1);
  and and_2 (and_2_out, A1, B1);
  xor xor_3 (xor_3_out, A2, B2);
  and and_3 (and_3_out, A2, B2);
  xor xor_4 (xor_4_out, A3, B3);
  and and_4 (and_4_out, A3, B3);
  and and_5 (and_5_out, C0, xor_1_out);
  and and_6 (and_6_out, C0, xor_1_out, xor_2_out);
  and and_7 (and_7_out, and_1_out, xor_2_out);
  and and_8 (and_8_out, C0, xor_1_out, xor_2_out, xor_3_out);
  and and_9 (and_9_out, and_1_out, xor_2_out, xor_3_out);
  and and_10 (and_10_out, and_2_out, xor_3_out);
  and and_11 (and_11_out, C0, xor_1_out, xor_2_out, xor_3_out, xor_4_out);
  and and_12 (and_12_out, and_1_out, xor_2_out, xor_3_out, xor_4_out);
  and and_13 (and_13_out, and_2_out, xor_3_out, xor_4_out);
  and and_14 (and_14_out, and_3_out, xor_4_out);
  or or_1 (or_1_out, and_5_out, and_1_out);
  or or_2 (or_2_out, and_6_out, and_7_out, and_2_out);
  or or_3 (or_3_out, and_8_out, and_9_out, and_10_out, and_3_out);
  or or_4 (C4, and_11_out, and_12_out, and_13_out, and_14_out, and_4_out);
  xor xor_5 (S0, C0, xor_1_out);
  xor xor_6 (S1, or_1_out, xor_2_out);
  xor xor_7 (S2, or_2_out, xor_3_out);
  xor xor_8 (S3, or_3_out, xor_4_out);
endmodule

module \new  (
  output out_1,
  output out_2,
  output out_3,
  output out_4,
  output out_5
);

  main main_1 (
    .C0(1'b1), .S0(out_4), .A0(1'b1), .B0(1'b1), .A1(1'b0), .S1(out_3), .B1(1'b0), .A2(1'b1), .S2(out_2),
    .B2(1'b1), .A3(1'b0), .S3(out_1), .B3(1'b0), .C4(out_5));
endmodule
