// Logisim project 2-1.circ as structural Verilog: 2 circuits, main circuit main
module main (
  input  CLR,
  input  CPu,
  input  CPd,
  output QA,
  output QB,
  output QC,
  output QD
);

  wire and_1_out, and_2_out, and_3_out, and_4_out, and_5_out, and_6_out, d_ff_1_qn, d_ff_2_qn, d_ff_3_qn,
       d_ff_4_qn, or_1_out, or_2_out, or_3_out, or_4_out;

  and and_1 (and_1_out, CPd, d_ff_1_qn);
  and and_2 (and_2_out, CPu, QA);
  and and_3 (and_3_out, CPd, d_ff_1_qn, d_ff_2_qn);
  and and_4 (and_4_out, CPu, QA, QB);
  and and_5 (and_5_out, CPd, d_ff_1_qn, d_ff_2_qn, d_ff_3_qn);
  and and_6 (and_6_out, CPu, QA, QB, QC);
  or or_1 (or_1_out, CPu, CPd);
  or or_2 (or_2_out, and_1_out, and_2_out);
  or or_3 (or_3_out, and_3_out, and_4_out);
  or or_4 (or_4_out, and_5_out, and_6_out);
  D_Flip_Flop #(.trigger("falling")) d_ff_1 (
    .clk(or_1_out), .D(d_ff_1_qn), .Q(QA), .Qn(d_ff_1_qn), .preset(1'b0), .en(1'b1), .reset(CLR));
  D_Flip_Flop #(.trigger("falling")) d_ff_2 (
    .clk(or_2_out), .D(d_ff_2_qn), .Q(QB), .Qn(d_ff_2_qn), .preset(1'b0), .en(1'b1), .reset(CLR));
  D_Flip_Flop #(.trigger("falling")) d_ff_3 (
    .clk(or_3_out), .D(d_ff_3_qn), .Q(QC), .Qn(d_ff_3_qn), .preset(1'b0), .en(1'b1), .reset(CLR));
  D_Flip_Flop #(.trigger("falling")) d_ff_4 (
    .clk(or_4_out), .D(d_ff_4_qn), .Q(QD), .Qn(d_ff_4_qn), .preset(1'b0), .en(1'b1), .reset(CLR));
endmodule

module test (
  input  in_1,
  input  in_2,
  input  in_3,
  output out_4,
  output out_5,
  output out_6,
  output out_7
);

  main main_1 (.CLR(in_2), .CPu(in_1), .CPd(in_3), .QA(out_7), .QB(out_6), .QC(out_5), .QD(out_4));
endmodule
