// Logisim project 2-2.circ as structural Verilog: 2 circuits, main circuit main
module main (
  input  D,
  input  C,
  input  B,
  input  A,
  output A7,
  output A6,
  output A5,
  output A4,
  output A3,
  output A2,
  output A1,
  output A0
);

  wire or_1_out;

  and and_1 (A4, or_1_out, D);
  or or_1 (or_1_out, C, B);
  _1_5_main main_1 (
    .C0(1'b0), .S0(A0), .A0(A), .B0(1'b0), .A1(B), .S1(A1), .B1(A4), .A2(C), .S2(A2), .B2(A4), .A3(D),
    .S3(A3), .B3(1'b0));  // open: C4

  assign A5 = 1'b0;
  assign A6 = 1'b0;
  assign A7 = 1'b0;
endmodule

module test (
  input  D,
  input  C,
  input  B,
  input  A,
  output A7,
  output A6,
  output A5,
  output A4,
  output A3,
  output A2,
  output A1,
  output A0
);

  main main_1 (.A7(A7), .A6(A6), .A5(A5), .A4(A4), .A3(A3), .A2(A2), .A1(A1), .A0(A0), .D(D), .C(C), .B(B), .A(A));
endmodule
