// Logisim project 2-3.circ as structural Verilog: 2 circuits, main circuit main
module main (
  input  A3,
  input  A2,
  input  A1,
  input  A0,
  output a,
  output b,
  output c,
  output d,
  output e,
  output f,
  output g
);

  wire and_1_out, and_2_out, and_3_out, and_4_out, and_6_out, and_7_out, nor_1_out, nor_2_out, nor_3_out,
       nor_5_out, not_1_out, not_2_out, or_4_out, or_6_out, xor_1_out, xor_2_out, xor_3_out;

  not not_1 (not_1_out, A2);
  and and_1 (and_1_out, not_1_out, A1);
  xor xor_1 (xor_1_out, A0, not_1_out);
  or or_1 (a, A3, xor_1_out, and_1_out);
  xor xor_2 (xor_2_out, A0, ~A1);  // XOR_Gate
  or or_2 (b, xor_2_out, ~A2, A3);  // OR_Gate
  or or_3 (c, A0, ~A1, A2);  // OR_Gate
  not not_2 (not_2_out, A0);
  or or_4 (or_4_out, not_2_out, A1);
  and and_2 (and_2_out, A1, not_2_out);
  xor xor_3 (xor_3_out, or_4_out, A2);
  or or_5 (d, and_2_out, xor_3_out);
  and and_3 (and_3_out, A1, A3);
  and and_4 (and_4_out, A1, A2, ~A3);  // AND_Gate
  nor nor_1 (nor_1_out, and_3_out, A2);
  or or_6 (or_6_out, and_4_out, nor_1_out);
  and and_5 (e, ~A0, or_6_out);  // AND_Gate
  nor nor_2 (nor_2_out, A0, A1);
  nor nor_3 (nor_3_out, A2, A3, nor_2_out);
  nor nor_4 (f, nor_3_out, and_6_out);
  nor nor_5 (nor_5_out, A1, A2, A3);
  and and_6 (and_6_out, A0, A1, A2);
  nor nor_6 (g, nor_5_out, and_7_out);
  and and_7 (and_7_out, A0, A1, A2);
endmodule

module display (
  input  A3,
  input  A2,
  input  A1,
  input  A0
);

  wire main_1_a, main_1_b, main_1_c, main_1_d, main_1_e, main_1_f, main_1_g;

  _7_Segment_Display u_7_segment_display_1 (
    .g(main_1_g), .f(main_1_f), .a(main_1_a), .b(main_1_b), .e(main_1_e), .d(main_1_d), .c(main_1_c));  // open: dp
  main main_1 (
    .A3(A3), .A2(A2), .A1(A1), .A0(A0), .a(main_1_a), .b(main_1_b), .c(main_1_c), .d(main_1_d), .e(main_1_e),
    .f(main_1_f), .g(main_1_g));
endmodule
