// Logisim project 2-4.circ as structural Verilog: 1 circuit, main circuit main
module main (
  input  CPu,
  input  CLR,
  input  CPd,
  output Alert,
  output QD,
  output QC,
  output QB,
  output QA
);

  wire and_1_out, and_2_out, buffer_1_out, buffer_2_out, or_1_out;

  buf buffer_1 (buffer_1_out, CPd);
  buf buffer_2 (buffer_2_out, CPu);
  and and_1 (and_1_out, ~Alert, buffer_2_out);  // AND_Gate
  and and_2 (and_2_out, buffer_1_out, or_1_out);
  _2_1_main main_1 (.CLR(CLR), .CPu(and_1_out), .CPd(and_2_out), .QA(QA), .QB(QB), .QC(QC), .QD(QD));
  or or_1 (or_1_out, QD, QC, QB, QA, ~CPd);  // OR_Gate
  and and_3 (Alert, CPu, QD, QC, QB, QA);
endmodule
