// Logisim project 2-5.circ as structural Verilog: 2 circuits, main circuit main
module main (
  input  CPu,
  input  CLR,
  input  CPd,
  output Alert,
  output a,
  output b,
  output c,
  output d,
  output e,
  output f,
  output g,
  output a_2,
  output b_2,
  output c_2,
  output d_2,
  output e_2,
  output f_2,
  output g_2
);

  wire main_1_qa, main_1_qb, main_1_qc, main_1_qd, main_3_a0, main_3_a1, main_3_a2, main_3_a3, main_3_a4,
       main_3_a5, main_3_a6, main_3_a7;

  _2_4_main main_1 (
    .CPu(CPu), .CLR(CLR), .CPd(CPd), .Alert(Alert), .QD(main_1_qd), .QC(main_1_qc), .QB(main_1_qb),
    .QA(main_1_qa));
  _2_3_main main_2 (
    .A3(main_3_a7), .A2(main_3_a6), .A1(main_3_a5), .A0(main_3_a4), .a(a), .b(b), .c(c), .d(d), .e(e), .f(f),
    .g(g));
  _2_2_main main_3 (
    .A7(main_3_a7), .A6(main_3_a6), .A5(main_3_a5), .A4(main_3_a4), .A3(main_3_a3), .A2(main_3_a2),
    .A1(main_3_a1), .A0(main_3_a0), .D(main_1_qd), .C(main_1_qc), .B(main_1_qb), .A(main_1_qa));
  _2_3_main main_4 (
    .A3(main_3_a3), .A2(main_3_a2), .A1(main_3_a1), .A0(main_3_a0), .a(a_2), .b(b_2), .c(c_2), .d(d_2),
    .e(e_2), .f(f_2), .g(g_2));
endmodule

module test (
  input  CPu,
  input  CLR,
  input  CPd,
  output out_4
);

  wire main_1_a, main_1_a_2, main_1_b, main_1_b_2, main_1_c, main_1_c_2, main_1_d, main_1_d_2, main_1_e,
       main_1_e_2, main_1_f, main_1_f_2, main_1_g, main_1_g_2;

  main main_1 (
    .CPu(CPu), .CLR(CLR), .CPd(CPd), .Alert(out_4), .a(main_1_a), .b(main_1_b), .c(main_1_c), .d(main_1_d),
    .e(main_1_e), .f(main_1_f), .g(main_1_g), .a_2(main_1_a_2), .b_2(main_1_b_2), .c_2(main_1_c_2),
    .d_2(main_1_d_2), .e_2(main_1_e_2), .f_2(main_1_f_2), .g_2(main_1_g_2));
  _7_Segment_Display u_7_segment_display_1 (
    .g(main_1_g), .f(main_1_f), .a(main_1_a), .b(main_1_b), .e(main_1_e), .d(main_1_d), .c(main_1_c));  // open: dp
  _7_Segment_Display u_7_segment_display_2 (
    .g(main_1_g_2), .f(main_1_f_2), .a(main_1_a_2), .b(main_1_b_2), .e(main_1_e_2), .d(main_1_d_2),
    .c(main_1_c_2));  // open: dp
endmodule
