// Logisim project 1-1.circ as structural Verilog: 1 circuit, main circuit main
module main (
  input  [3:0] a,
  input  [3:0] b,
  output [7:0] p
);

  wire [7:0] adder_1_out, adder_2_out, adder_3_out, adder_4_out, multiplexer_1_out, multiplexer_2_out,
       multiplexer_3_out;

  // Probe on b
  // Probe on a
  Multiplexer #(.width(8), .enable("false")) multiplexer_1 (
    .in0({8{1'b0}}), .in1(adder_1_out), .out(multiplexer_1_out), .sel(a[0]));
  Adder adder_1 (.a({8{1'b0}}), .b({4'b0000, b}), .out(adder_1_out));  // open: cin, cout
  Adder adder_2 (.a(multiplexer_1_out), .b({3'b000, b, 1'b0}), .out(adder_2_out));  // open: cin, cout
  Multiplexer #(.width(8), .enable("false")) multiplexer_2 (
    .in0(multiplexer_1_out), .in1(adder_2_out), .out(multiplexer_2_out), .sel(a[1]));
  Adder adder_3 (.a(multiplexer_2_out), .b({2'b00, b, 2'b00}), .out(adder_3_out));  // open: cin, cout
  Multiplexer #(.width(8), .enable("false")) multiplexer_3 (
    .in0(multiplexer_2_out), .in1(adder_3_out), .out(multiplexer_3_out), .sel(a[2]));
  Adder adder_4 (.a(multiplexer_3_out), .b({1'b0, b, 3'b000}), .out(adder_4_out));  // open: cin, cout
  Multiplexer #(.width(8), .enable("false")) multiplexer_4 (
    .in0(multiplexer_3_out), .in1(adder_4_out), .out(p), .sel(a[3]));
  // Probe on p
endmodule
