// Logisim project 1-2.circ as structural Verilog: 1 circuit, main circuit main
module main (
  input  [3:0] a,
  input  [31:0] b,
  output [31:0] p
);

  wire [31:0] adder_1_out, adder_2_out, adder_3_out, adder_4_out, multiplexer_1_out, multiplexer_2_out,
       multiplexer_3_out;

  // Probe on a
  // Probe on b
  Multiplexer #(.width(32), .enable("false")) multiplexer_1 (
    .in0({32{1'b0}}), .in1(adder_1_out), .out(multiplexer_1_out), .sel(a[0]));
  Adder #(.width(32)) adder_1 (.a({32{1'b0}}), .b(b), .out(adder_1_out));  // open: cin, cout
  Adder #(.width(32)) adder_2 (.a(multiplexer_1_out), .b({b[30:0], 1'b0}), .out(adder_2_out));  // open: cin, cout
  Multiplexer #(.width(32), .enable("false")) multiplexer_2 (
    .in0(multiplexer_1_out), .in1(adder_2_out), .out(multiplexer_2_out), .sel(a[1]));
  Multiplexer #(.width(32), .enable("false")) multiplexer_3 (
    .in0(multiplexer_2_out), .in1(adder_3_out), .out(multiplexer_3_out), .sel(a[2]));
  Adder #(.width(32)) adder_3 (.a(multiplexer_2_out), .b({b[29:0], 2'b00}), .out(adder_3_out));  // open: cin, cout
  Adder #(.width(32)) adder_4 (.a(multiplexer_3_out), .b({b[28:0], 3'b000}), .out(adder_4_out));  // open: cin, cout
  Multiplexer #(.width(32), .enable("false")) multiplexer_4 (
    .in0(multiplexer_3_out), .in1(adder_4_out), .out(p), .sel(a[3]));
  // Probe on p
endmodule
