// Logisim project 1-3.circ as structural Verilog: 1 circuit, main circuit main
module main (
  input  [31:0] a,
  input  [31:0] b,
  output [31:0] p
);

  wire [31:0] adder_1_out, adder_2_out, adder_3_out, adder_4_out, adder_5_out, adder_6_out, main_1_p3,
       main_2_p3, main_3_p3, main_4_p3, main_5_p3, main_6_p3, main_7_p3, main_8_p3, shifter_1_out,
       shifter_2_out, shifter_3_out, shifter_4_out, shifter_5_out, shifter_6_out, shifter_7_out,
       shifter_8_out;

  // Probe on a
  // Probe on b
  // _1_2_main main_1: pin names not known; wires that end beside it: a[3:0], b, main_1_p3
  // _1_2_main main_2: pin names not known; wires that end beside it: a[7:4], b, main_2_p3
  // _1_2_main main_3: pin names not known; wires that end beside it: a[11:8], b, main_3_p3
  // _1_2_main main_4: pin names not known; wires that end beside it: a[15:12], b, main_4_p3
  // _1_2_main main_5: pin names not known; wires that end beside it: a[19:16], b, main_5_p3
  // _1_2_main main_6: pin names not known; wires that end beside it: a[23:20], b, main_6_p3
  // _1_2_main main_7: pin names not known; wires that end beside it: a[27:24], b, main_7_p3
  // _1_2_main main_8: pin names not known; wires that end beside it: a[31:28], b, main_8_p3
  Shifter #(.width(32)) shifter_1 (.in(main_1_p3), .\dist ({5{1'b0}}), .out(shifter_1_out));
  Shifter #(.width(32)) shifter_2 (.in(main_2_p3), .\dist (5'b00100), .out(shifter_2_out));
  Shifter #(.width(32)) shifter_3 (.in(main_3_p3), .\dist (5'b01000), .out(shifter_3_out));
  Shifter #(.width(32)) shifter_4 (.in(main_4_p3), .\dist (5'b01100), .out(shifter_4_out));
  Shifter #(.width(32)) shifter_5 (.in(main_5_p3), .\dist (5'b10000), .out(shifter_5_out));
  Shifter #(.width(32)) shifter_6 (.in(main_6_p3), .\dist (5'b10100), .out(shifter_6_out));
  Shifter #(.width(32)) shifter_7 (.in(main_7_p3), .\dist (5'b11000), .out(shifter_7_out));
  Shifter #(.width(32)) shifter_8 (.in(main_8_p3), .\dist (5'b11100), .out(shifter_8_out));
  Adder #(.width(32)) adder_1 (.a(shifter_1_out), .b(shifter_2_out), .out(adder_1_out));  // open: cin, cout
  Adder #(.width(32)) adder_2 (.a(adder_1_out), .b(shifter_3_out), .out(adder_2_out));  // open: cin, cout
  Adder #(.width(32)) adder_3 (.a(adder_2_out), .b(shifter_4_out), .out(adder_3_out));  // open: cin, cout
  Adder #(.width(32)) adder_4 (.a(adder_3_out), .b(shifter_5_out), .out(adder_4_out));  // open: cin, cout
  Adder #(.width(32)) adder_5 (.a(adder_4_out), .b(shifter_6_out), .out(adder_5_out));  // open: cin, cout
  Adder #(.width(32)) adder_6 (.a(adder_5_out), .b(shifter_7_out), .out(adder_6_out));  // open: cin, cout
  Adder #(.width(32)) adder_7 (.a(adder_6_out), .b(shifter_8_out), .out(p));  // open: cin, cout
  // Probe on p
endmodule
