// Logisim project 2-1.circ as structural Verilog: 1 circuit, main circuit main
module main (
  input  [3:0] n2,
  input  [3:0] d,
  output [3:0] quot,
  output [3:0] rem
);

  wire comparator_1_lt, comparator_2_lt, comparator_3_lt, comparator_4_lt;
  wire [3:0] multiplexer_1_out, multiplexer_2_out, multiplexer_3_out, subtractor_1_out, subtractor_2_out,
       subtractor_3_out, subtractor_4_out;

  // Probe on n2
  // Probe on d
  Subtractor #(.width(4)) subtractor_1 (.a({3'b000, n2[3]}), .b(d), .out(subtractor_1_out));  // open: bin, bout
  Comparator #(.width(4), .mode("unsigned")) comparator_1 (
    .a({3'b000, n2[3]}), .b(d), .lt(comparator_1_lt));  // open: gt, eq
  Multiplexer #(.width(4), .enable("false")) multiplexer_1 (
    .in0({3'b000, n2[3]}), .in1(subtractor_1_out), .out(multiplexer_1_out), .sel(quot[3]));
  not not_1 (quot[3], comparator_1_lt);
  Subtractor #(.width(4)) subtractor_2 (
    .a({multiplexer_1_out[2:0], n2[2]}), .b(d), .out(subtractor_2_out));  // open: bin, bout
  Comparator #(.width(4), .mode("unsigned")) comparator_2 (
    .a({multiplexer_1_out[2:0], n2[2]}), .b(d), .lt(comparator_2_lt));  // open: gt, eq
  not not_2 (quot[2], comparator_2_lt);
  Multiplexer #(.width(4), .enable("false")) multiplexer_2 (
    .in0({multiplexer_1_out[2:0], n2[2]}), .in1(subtractor_2_out), .out(multiplexer_2_out), .sel(quot[2]));
  Subtractor #(.width(4)) subtractor_3 (
    .a({multiplexer_2_out[2:0], n2[1]}), .b(d), .out(subtractor_3_out));  // open: bin, bout
  Comparator #(.width(4), .mode("unsigned")) comparator_3 (
    .a({multiplexer_2_out[2:0], n2[1]}), .b(d), .lt(comparator_3_lt));  // open: gt, eq
  not not_3 (quot[1], comparator_3_lt);
  Multiplexer #(.width(4), .enable("false")) multiplexer_3 (
    .in0({multiplexer_2_out[2:0], n2[1]}), .in1(subtractor_3_out), .out(multiplexer_3_out), .sel(quot[1]));
  Subtractor #(.width(4)) subtractor_4 (
    .a({multiplexer_3_out[2:0], n2[0]}), .b(d), .out(subtractor_4_out));  // open: bin, bout
  Comparator #(.width(4), .mode("unsigned")) comparator_4 (
    .a({multiplexer_3_out[2:0], n2[0]}), .b(d), .lt(comparator_4_lt));  // open: gt, eq
  not not_4 (quot[0], comparator_4_lt);
  Multiplexer #(.width(4), .enable("false")) multiplexer_4 (
    .in0({multiplexer_3_out[2:0], n2[0]}), .in1(subtractor_4_out), .out(rem), .sel(quot[0]));
  // Probe on quot
  // Probe on rem
endmodule
