// Logisim project 2-2.circ as structural Verilog: 3 circuits, main circuit main
module four (
  input  [31:0] n2_in,
  input  [31:0] n1_in,
  input  [31:0] d,
  output [31:0] n2_out,
  output [31:0] n1_out
);

  wire [31:0] buffer_1_out, buffer_2_out, buffer_3_out, buffer_4_out, buffer_5_out, buffer_6_out,
       buffer_7_out, buffer_8_out, buffer_9_out, one_1_n1_out, one_1_n2_out, one_2_n1_out, one_2_n2_out,
       one_3_n1_out, one_3_n2_out;

  assign buffer_1_out = d;  // Buffer buffer_1, 32 bits wide
  one one_1 (.n2_in(n2_in), .n1_in(n1_in), .d(d), .n1_out(one_1_n1_out), .n2_out(one_1_n2_out));
  assign buffer_2_out = buffer_1_out;  // Buffer buffer_2, 32 bits wide
  assign buffer_3_out = buffer_2_out;  // Buffer buffer_3, 32 bits wide
  one one_2 (
    .n2_in(one_1_n2_out), .n1_in(one_1_n1_out), .d(buffer_3_out), .n1_out(one_2_n1_out), .n2_out(one_2_n2_out));
  assign buffer_4_out = buffer_6_out;  // Buffer buffer_4, 32 bits wide
  assign buffer_5_out = buffer_4_out;  // Buffer buffer_5, 32 bits wide
  assign buffer_6_out = buffer_3_out;  // Buffer buffer_6, 32 bits wide
  one one_3 (
    .n2_in(one_2_n2_out), .n1_in(one_2_n1_out), .d(buffer_5_out), .n1_out(one_3_n1_out), .n2_out(one_3_n2_out));
  assign buffer_7_out = buffer_5_out;  // Buffer buffer_7, 32 bits wide
  assign buffer_8_out = buffer_7_out;  // Buffer buffer_8, 32 bits wide
  assign buffer_9_out = buffer_8_out;  // Buffer buffer_9, 32 bits wide
  one one_4 (.n2_in(one_3_n2_out), .n1_in(one_3_n1_out), .d(buffer_9_out), .n1_out(n1_out), .n2_out(n2_out));
endmodule

module one (
  input  [31:0] n2_in,
  input  [31:0] n1_in,
  input  [31:0] d,
  output [31:0] n2_out,
  output [31:0] n1_out
);

  wire comparator_1_eq, comparator_2_lt, not_1_out, not_2_out;
  wire [30:0] buffer_2_out, buffer_3_out;
  wire [31:0] buffer_4_out, buffer_5_out, buffer_6_out, demultiplexer_1_out1, subtractor_1_out;

  Demultiplexer #(.width(32), .enable("false")) demultiplexer_1 (
    .out1(demultiplexer_1_out1), .in(n2_in), .sel(not_1_out));  // open: out0
  not not_1 (not_1_out, comparator_1_eq);
  Comparator #(.width(32), .mode("unsigned")) comparator_1 (
    .a(n2_in), .b({32{1'b0}}), .eq(comparator_1_eq));  // open: gt, lt
  assign n2_out[31:1] = buffer_2_out;  // Buffer buffer_1, 31 bits wide
  assign buffer_2_out = buffer_3_out;  // Buffer buffer_2, 31 bits wide
  assign buffer_3_out = demultiplexer_1_out1[30:0];  // Buffer buffer_3, 31 bits wide
  assign buffer_4_out = {n1_in[30:0], demultiplexer_1_out1[31]};  // Buffer buffer_4, 32 bits wide
  Subtractor #(.width(32)) subtractor_1 (
    .a({n1_in[30:0], demultiplexer_1_out1[31]}), .b(d), .out(subtractor_1_out));  // open: bin, bout
  Comparator #(.width(32), .mode("unsigned")) comparator_2 (
    .a({n1_in[30:0], demultiplexer_1_out1[31]}), .b(d), .lt(comparator_2_lt));  // open: gt, eq
  assign buffer_5_out = buffer_4_out;  // Buffer buffer_5, 32 bits wide
  assign buffer_6_out = subtractor_1_out;  // Buffer buffer_6, 32 bits wide
  not not_2 (not_2_out, comparator_2_lt);
  buf buffer_7 (n2_out[0], not_2_out);
  Multiplexer #(.width(32), .enable("false")) multiplexer_1 (
    .in0(buffer_5_out), .in1(buffer_6_out), .out(n1_out), .sel(not_2_out));
endmodule

module main (
  input  [31:0] n2,
  input  [31:0] d,
  output [31:0] quot,
  output [31:0] rem
);

  wire [31:0] four_1_n1_out, four_1_n2_out, four_2_n1_out, four_2_n2_out, four_3_n1_out, four_3_n2_out,
       four_4_n1_out, four_4_n2_out, four_5_n1_out, four_5_n2_out, four_6_n1_out, four_6_n2_out,
       four_7_n1_out, four_7_n2_out;

  // Probe on n2
  // Probe on d
  four four_1 (.n2_in(n2), .n1_in({32{1'b0}}), .d(d), .n2_out(four_1_n2_out), .n1_out(four_1_n1_out));
  four four_2 (.n2_in(four_1_n2_out), .n1_in(four_1_n1_out), .d(d), .n2_out(four_2_n2_out), .n1_out(four_2_n1_out));
  four four_3 (.n2_in(four_2_n2_out), .n1_in(four_2_n1_out), .d(d), .n2_out(four_3_n2_out), .n1_out(four_3_n1_out));
  four four_4 (.n2_in(four_3_n2_out), .n1_in(four_3_n1_out), .d(d), .n2_out(four_4_n2_out), .n1_out(four_4_n1_out));
  four four_5 (.n2_in(four_4_n2_out), .n1_in(four_4_n1_out), .d(d), .n2_out(four_5_n2_out), .n1_out(four_5_n1_out));
  four four_6 (.n2_in(four_5_n2_out), .n1_in(four_5_n1_out), .d(d), .n2_out(four_6_n2_out), .n1_out(four_6_n1_out));
  four four_7 (.n2_in(four_6_n2_out), .n1_in(four_6_n1_out), .d(d), .n2_out(four_7_n2_out), .n1_out(four_7_n1_out));
  // Probe on quot
  four four_8 (.n2_in(four_7_n2_out), .n1_in(four_7_n1_out), .d(d), .n2_out(quot), .n1_out(rem));
  // Probe on rem
endmodule
