// Logisim project 1.circ as structural Verilog: 15 circuits, main circuit Main
module m16_Counter (
  input  CLR,
  input  CPu,
  input  CPd,
  input  A0,
  input  A1,
  input  A2,
  input  A3,
  output Q0,
  output Q1,
  output Q2,
  output Q3
);

  wire and_1_out, and_2_out, and_3_out, and_4_out, and_5_out, and_6_out, d_ff_1_qn, d_ff_2_qn, d_ff_3_qn,
       d_ff_4_qn, or_1_out, or_2_out, or_3_out, or_4_out;

  and and_1 (and_1_out, CPd, d_ff_1_qn);
  and and_2 (and_2_out, CPu, Q0);
  and and_3 (and_3_out, CPd, d_ff_1_qn, d_ff_2_qn);
  and and_4 (and_4_out, CPu, Q0, Q1);
  and and_5 (and_5_out, CPd, d_ff_1_qn, d_ff_2_qn, d_ff_3_qn);
  and and_6 (and_6_out, CPu, Q0, Q1, Q2);
  or or_1 (or_1_out, CPu, A0, CPd);
  or or_2 (or_2_out, and_1_out, A1, and_2_out);
  or or_3 (or_3_out, and_3_out, A2, and_4_out);
  or or_4 (or_4_out, and_5_out, A3, and_6_out);
  D_Flip_Flop #(.trigger("falling")) d_ff_1 (
    .clk(or_1_out), .D(d_ff_1_qn), .Q(Q0), .Qn(d_ff_1_qn), .preset(1'b0), .en(1'b1), .reset(CLR));
  D_Flip_Flop #(.trigger("falling")) d_ff_2 (
    .clk(or_2_out), .D(d_ff_2_qn), .Q(Q1), .Qn(d_ff_2_qn), .preset(1'b0), .en(1'b1), .reset(CLR));
  D_Flip_Flop #(.trigger("falling")) d_ff_3 (
    .clk(or_3_out), .D(d_ff_3_qn), .Q(Q2), .Qn(d_ff_3_qn), .preset(1'b0), .en(1'b1), .reset(CLR));
  D_Flip_Flop #(.trigger("falling")) d_ff_4 (
    .clk(or_4_out), .D(d_ff_4_qn), .Q(Q3), .Qn(d_ff_4_qn), .preset(1'b0), .en(1'b1), .reset(CLR));
endmodule

module m10_Counter (
  input  CLR,
  input  CPu,
  input  CPd,
  output carry,
  output borrow,
  output Q3,
  output Q2,
  output Q1,
  output Q0
);

  wire and_1_out, buffer_1_out, not_1_out, not_2_out, or_1_out, or_2_out;

  buf buffer_1 (buffer_1_out, CPd);
  or or_1 (or_1_out, carry, CLR);
  and and_1 (and_1_out, buffer_1_out, or_2_out);
  not not_1 (not_1_out, or_2_out);
  m16_Counter m16_counter_1 (
    .CLR(or_1_out), .CPu(CPu), .CPd(and_1_out), .Q0(Q0), .Q1(Q1), .Q2(Q2), .Q3(Q3), .A0(not_1_out),
    .A1(1'b0), .A2(1'b0), .A3(not_2_out));
  not not_2 (not_2_out, or_2_out);
  and and_2 (carry, Q1, Q3);
  or or_2 (or_2_out, ~CPd, Q3, Q2, Q1, Q0);  // OR_Gate
  not not_3 (borrow, or_2_out);
endmodule

module m6_Counter (
  input  CLR,
  input  CPu,
  input  CPd,
  output carry,
  output borrow,
  output Q3,
  output Q2,
  output Q1,
  output Q0
);

  wire and_1_out, buffer_1_out, not_1_out, not_2_out, or_1_out, or_2_out;

  buf buffer_1 (buffer_1_out, CPd);
  or or_1 (or_1_out, carry, CLR);
  and and_1 (and_1_out, buffer_1_out, or_2_out);
  not not_1 (not_1_out, or_2_out);
  m16_Counter m16_counter_1 (
    .CLR(or_1_out), .CPu(CPu), .CPd(and_1_out), .Q0(Q0), .Q1(Q1), .Q2(Q2), .Q3(Q3), .A0(not_1_out),
    .A1(1'b0), .A2(not_2_out), .A3(1'b0));
  not not_2 (not_2_out, or_2_out);
  and and_2 (carry, Q1, Q2);
  or or_2 (or_2_out, ~CPd, Q3, Q2, Q1, Q0);  // OR_Gate
  not not_3 (borrow, or_2_out);
endmodule

module m60_Counter (
  input  CLR,
  input  CP,
  input  CPu,
  input  Adj,
  input  CPd,
  output [3:0] Q1,
  output ca,
  output bo,
  output [3:0] Q0
);

  wire m10_counter_1_borrow, m10_counter_1_carry, multiplexer_1_out, multiplexer_2_out;

  Multiplexer #(.enable("false")) multiplexer_1 (.in0(CP), .in1(CPu), .out(multiplexer_1_out), .sel(Adj));
  Multiplexer #(.enable("false")) multiplexer_2 (.in0(1'b0), .in1(CPd), .out(multiplexer_2_out), .sel(Adj));
  m6_Counter m6_counter_1 (
    .CLR(CLR), .CPu(m10_counter_1_carry), .CPd(m10_counter_1_borrow), .carry(ca), .Q3(Q1[3]), .Q2(Q1[2]),
    .Q1(Q1[1]), .Q0(Q1[0]), .borrow(bo));
  m10_Counter m10_counter_1 (
    .Q0(Q0[0]), .Q1(Q0[1]), .Q2(Q0[2]), .Q3(Q0[3]), .CPu(multiplexer_1_out), .CPd(multiplexer_2_out),
    .carry(m10_counter_1_carry), .borrow(m10_counter_1_borrow), .CLR(CLR));
endmodule

module Hour_Converter (
  input  Q7,
  input  Q6,
  input  Q5,
  input  Q4,
  input  Q3,
  input  Q2,
  input  Q1,
  input  Q0,
  output [3:0] D1,
  output [3:0] D0
);

  wire and_3_out, and_4_out, or_1_out, or_2_out;

  // Probe on {2'b00, D1[1:0]}
  and and_1 (D1[1], Q2, Q4);
  and and_2 (D1[0], ~D1[1], or_1_out);  // AND_Gate
  or or_1 (or_1_out, Q4, and_4_out, and_3_out);
  _1_5_main main_1 (
    .C0(1'b0), .S0(D0[0]), .A0(Q0), .B0(1'b0), .A1(Q1), .S1(D0[1]), .B1(D1[0]), .A2(Q2), .S2(D0[2]),
    .B2(or_2_out), .A3(Q3), .S3(D0[3]), .B3(D1[1]));  // open: C4
  and and_3 (and_3_out, Q1, Q3);
  and and_4 (and_4_out, Q3, Q2);
  // Probe on D0
  or or_2 (or_2_out, D1[1], D1[0]);

  assign D1[3:2] = 2'b00;
endmodule

module m12_24_Counter (
  input  CLR,
  input  CP,
  input  CPu,
  input  Adj,
  input  CPd,
  input  SET,
  output [3:0] Q1,
  output [3:0] Q0,
  output ch,
  output ca,
  output bo
);

  wire and_1_out, and_2_out, m6_counter_1_borrow, m6_counter_1_carry, multiplexer_1_out, multiplexer_2_out,
       multiplexer_3_out;
  wire [1:0] m2_4_counter_1_q0;
  wire [2:0] m6_counter_1_q0;
  wire [7:0] adder_1_out, main_1_p;

  Multiplexer #(.enable("false")) multiplexer_1 (.in0(CP), .in1(CPu), .out(multiplexer_1_out), .sel(Adj));
  Multiplexer #(.enable("false")) multiplexer_2 (.in0(1'b0), .in1(CPd), .out(multiplexer_2_out), .sel(Adj));
  m6_Counter m6_counter_1 (
    .CLR(CLR), .CPu(multiplexer_1_out), .CPd(multiplexer_2_out), .carry(m6_counter_1_carry),
    .Q2(m6_counter_1_q0[2]), .Q1(m6_counter_1_q0[1]), .Q0(m6_counter_1_q0[0]), .borrow(m6_counter_1_borrow));  // open: Q3
  m2_4_Counter m2_4_counter_1 (
    .CPu(m6_counter_1_carry), .CPd(m6_counter_1_borrow), .CLR(CLR), .ch(ch), .Q1(m2_4_counter_1_q0[1]),
    .Q0(m2_4_counter_1_q0[0]), .SET(SET));
  Multiplexer #(.enable("false")) multiplexer_3 (
    .in0(1'b0), .in1(m2_4_counter_1_q0[1]), .out(multiplexer_3_out), .sel(SET));
  _1_1_main main_1 (.a(4'b0110), .b({2'b00, m2_4_counter_1_q0}), .p(main_1_p));
  and and_1 (and_1_out, SET, multiplexer_3_out, m2_4_counter_1_q0[0], m6_counter_1_carry);
  and and_2 (and_2_out, m6_counter_1_carry, ~SET, m2_4_counter_1_q0[0]);  // AND_Gate
  nor nor_1 (bo, multiplexer_3_out, ~m6_counter_1_borrow, m2_4_counter_1_q0[0]);  // NOR_Gate
  Adder adder_1 (.a({{5{1'b0}}, m6_counter_1_q0}), .b(main_1_p), .out(adder_1_out));  // open: cin, cout
  or or_1 (ca, and_1_out, and_2_out);
  Hour_Converter hour_converter_1 (
    .D1(Q1), .D0(Q0), .Q7(adder_1_out[7]), .Q6(adder_1_out[6]), .Q5(adder_1_out[5]), .Q4(adder_1_out[4]),
    .Q3(adder_1_out[3]), .Q2(adder_1_out[2]), .Q1(adder_1_out[1]), .Q0(adder_1_out[0]));
endmodule

module m2_4_Counter (
  input  CPu,
  input  CPd,
  input  CLR,
  input  SET,
  output Q0,
  output ch,
  output Q1
);

  wire and_1_out, and_2_out, or_1_out, or_2_out, or_3_out, t_ff_2_qn;

  and and_1 (and_1_out, Q0, CPu);
  and and_2 (and_2_out, CPd, t_ff_2_qn);
  or or_1 (or_1_out, CPu, CPd);
  or or_2 (or_2_out, and_1_out, and_2_out);
  or or_3 (or_3_out, or_2_out, 1'b0);
  T_Flip_Flop #(.trigger("falling")) t_ff_1 (.clk(or_3_out), .T(1'b1), .Q(ch), .reset(CLR));  // open: Qn, preset, en
  T_Flip_Flop #(.trigger("falling")) t_ff_2 (
    .clk(or_1_out), .T(1'b1), .Q(Q0), .Qn(t_ff_2_qn), .reset(CLR));  // open: preset, en
  and and_3 (Q1, ch, SET);
endmodule

module am_pm (
  input  AM_PM,
  input  TT,
  output [4:0] Q3,
  output [4:0] Q2,
  output [4:0] Q1,
  output [4:0] Q0
);

  Multiplexer #(.width(5)) multiplexer_1 (.in0(5'b00001), .in1(5'b10000), .out(Q3), .sel(AM_PM), .en(TT));
  Multiplexer #(.width(5)) multiplexer_2 (.in0({5{1'b1}}), .in1({5{1'b1}}), .out(Q2), .sel(AM_PM), .en(TT));
  Multiplexer #(.width(5)) multiplexer_3 (.in0(5'b00101), .in1(5'b10100), .out(Q1), .sel(AM_PM), .en(TT));
  Multiplexer #(.width(5)) multiplexer_4 (.in0(5'b00001), .in1(5'b10000), .out(Q0), .sel(AM_PM), .en(TT));
endmodule

module Hour_Alarm (
  input  [3:0] sec1,
  input  [3:0] min1,
  input  [3:0] min0,
  input  CP,
  output alarm
);

  and and_1 (alarm, sec1[0], sec1[2], min1[0], min1[2], min0[0], min0[3], CP);
endmodule

module _8Hz_to_1Hz (
  input  _8Hz,
  output _1Hz
);

  wire and_1_out, m2_4_counter_1_q0, m2_4_counter_1_q1;

  m2_4_Counter m2_4_counter_1 (
    .CPu(_8Hz), .CPd(1'b0), .CLR(1'b0), .Q1(m2_4_counter_1_q1), .Q0(m2_4_counter_1_q0), .SET(1'b1));  // open: ch
  and and_1 (and_1_out, m2_4_counter_1_q1, m2_4_counter_1_q0);
  m2_4_Counter m2_4_counter_2 (.CPu(and_1_out), .CPd(1'b0), .CLR(1'b0), .Q0(_1Hz), .SET(1'b0));  // open: ch, Q1
endmodule

module Main (
  input  CLR,
  input  Adj0,
  input  Adj1,
  input  CPu,
  input  CPd,
  input  CP,
  input  SET,
  output alarm,
  output [3:0] min0,
  output [3:0] sec1,
  output [3:0] sec0,
  output [3:0] min1,
  output [3:0] hour1,
  output [3:0] hour0,
  output am_pm
);

  wire m12_24_counter_1_bo, m12_24_counter_1_ch, m60_counter_1_bo, m60_counter_1_ca, m60_counter_2_bo,
       m60_counter_2_ca, multiplexer_1_out, multiplexer_2_out, multiplexer_3_out, multiplexer_4_out,
       multiplexer_5_out, multiplexer_6_out, multiplexer_7_out, multiplexer_8_out, n8hz_to_1hz_1__1hz,
       not_1_out, not_2_out;

  _8Hz_to_1Hz u_8hz_to_1hz_1 (._8Hz(CP), ._1Hz(n8hz_to_1hz_1__1hz));
  m60_Counter m60_counter_1 (
    .CLR(CLR), .CP(n8hz_to_1hz_1__1hz), .CPu(1'b0), .Adj(1'b0), .CPd(1'b0), .ca(m60_counter_1_ca),
    .bo(m60_counter_1_bo), .Q1(sec1), .Q0(sec0));
  Multiplexer #(.enable("false")) multiplexer_1 (
    .in0(m60_counter_1_ca), .in1(CPu), .out(multiplexer_1_out), .sel(Adj1));
  Multiplexer #(.enable("false")) multiplexer_2 (
    .in0(m60_counter_1_bo), .in1(CPd), .out(multiplexer_2_out), .sel(Adj1));
  Multiplexer #(.enable("false")) multiplexer_3 (
    .in0(1'b0), .in1(multiplexer_1_out), .out(multiplexer_3_out), .sel(not_1_out));
  Multiplexer #(.enable("false")) multiplexer_4 (
    .in0(1'b0), .in1(multiplexer_2_out), .out(multiplexer_4_out), .sel(not_1_out));
  not not_1 (not_1_out, Adj0);
  m12_24_Counter m12_24_counter_1 (
    .CLR(CLR), .CP(1'b0), .CPu(multiplexer_7_out), .Adj(1'b1), .CPd(multiplexer_8_out),
    .ch(m12_24_counter_1_ch), .bo(m12_24_counter_1_bo), .Q1(hour1), .Q0(hour0), .SET(SET));  // open: ca
  m60_Counter m60_counter_2 (
    .CLR(CLR), .CP(1'b0), .CPu(multiplexer_3_out), .Adj(1'b1), .CPd(multiplexer_4_out),
    .ca(m60_counter_2_ca), .bo(m60_counter_2_bo), .Q1(min1), .Q0(min0));
  or or_1 (am_pm, m12_24_counter_1_ch, m12_24_counter_1_bo);
  Multiplexer #(.enable("false")) multiplexer_5 (
    .in0(m60_counter_2_ca), .in1(CPu), .out(multiplexer_5_out), .sel(Adj0));
  Multiplexer #(.enable("false")) multiplexer_6 (
    .in0(m60_counter_2_bo), .in1(CPd), .out(multiplexer_6_out), .sel(Adj0));
  not not_2 (not_2_out, Adj1);
  Hour_Alarm hour_alarm_1 (.CP(n8hz_to_1hz_1__1hz), .alarm(alarm), .sec1(sec1), .min1(min1), .min0(min0));
  Multiplexer #(.enable("false")) multiplexer_7 (
    .in0(1'b0), .in1(multiplexer_5_out), .out(multiplexer_7_out), .sel(not_2_out));
  Multiplexer #(.enable("false")) multiplexer_8 (
    .in0(1'b0), .in1(multiplexer_6_out), .out(multiplexer_8_out), .sel(not_2_out));
endmodule

module Clock (
  input  cam_pm,
  input  am_pm,
  input  SET,
  input  [3:0] h1,
  input  [3:0] s1,
  input  [3:0] m1,
  input  [3:0] h0,
  input  [3:0] cm1,
  input  [3:0] m0,
  input  CP,
  input  [3:0] cm0,
  input  [3:0] ch1,
  input  [3:0] ch0,
  output alarm
);

  wire and_1_out, comparator_1_eq, comparator_2_eq, comparator_3_eq, comparator_4_eq, comparator_5_lt,
       comparator_6_eq, comparator_7_eq, multiplexer_2_out;
  wire [7:0] adder_1_out, adder_2_out, bit_extender_1_out, bit_extender_2_out, main_1_p, main_2_p,
       multiplexer_1_out, subtractor_1_out;

  assign bit_extender_1_out = {{4{1'b0}}, h0};  // Bit_Extender bit_extender_1
  assign bit_extender_2_out = {{4{1'b0}}, ch0};  // Bit_Extender bit_extender_2
  _1_1_main main_1 (.a(h1), .b(4'b1010), .p(main_1_p));
  _1_1_main main_2 (.a(ch1), .b(4'b1010), .p(main_2_p));
  Adder adder_1 (.a(main_1_p), .b(bit_extender_1_out), .out(adder_1_out));  // open: cin, cout
  Adder adder_2 (.a(main_2_p), .b(bit_extender_2_out), .out(adder_2_out));  // open: cin, cout
  Multiplexer #(.width(8), .enable("false")) multiplexer_1 (
    .in0(adder_1_out), .in1(subtractor_1_out), .out(multiplexer_1_out), .sel(cam_pm));
  Subtractor subtractor_1 (.a(adder_1_out), .b(8'hc), .out(subtractor_1_out));  // open: bin, bout
  Comparator #(.width(1), .mode("unsigned")) comparator_1 (
    .a(cam_pm), .b(am_pm), .eq(comparator_1_eq));  // open: gt, lt
  Comparator #(.width(4), .mode("unsigned")) comparator_2 (.a(h1), .b(ch1), .eq(comparator_2_eq));  // open: gt, lt
  Comparator #(.width(4), .mode("unsigned")) comparator_3 (.a(h0), .b(ch0), .eq(comparator_3_eq));  // open: gt, lt
  Comparator comparator_4 (.a(multiplexer_1_out), .b(adder_2_out), .eq(comparator_4_eq));  // open: gt, lt
  and and_1 (and_1_out, comparator_1_eq, comparator_2_eq, comparator_3_eq);
  Multiplexer #(.enable("false")) multiplexer_2 (
    .in0(and_1_out), .in1(comparator_4_eq), .out(multiplexer_2_out), .sel(SET));
  Comparator #(.width(4), .mode("unsigned")) comparator_5 (.a(s1), .b(4'b0001), .lt(comparator_5_lt));  // open: gt, eq
  Comparator #(.width(4), .mode("unsigned")) comparator_6 (.a(m1), .b(cm1), .eq(comparator_6_eq));  // open: gt, lt
  Comparator #(.width(4), .mode("unsigned")) comparator_7 (.a(m0), .b(cm0), .eq(comparator_7_eq));  // open: gt, lt
  and and_2 (alarm, multiplexer_2_out, comparator_5_lt, comparator_6_eq, comparator_7_eq, CP);
endmodule

module Clock_Setter (
  input  Adjm,
  input  CPu,
  input  CPd,
  input  CLR,
  output am_pm,
  output oAdm,
  output [3:0] m1,
  output [3:0] m0,
  output [3:0] h1,
  output [3:0] h0,
  output CPu_2,
  output CPd_2,
  output CLR_2
);

  wire and_1_out, and_2_out, and_3_out, and_4_out, and_5_out, and_9_out, and_10_out, and_11_out, and_12_out,
       and_13_out, and_14_out, buffer_1_out, buffer_2_out, m2_4_counter_1_q0, m2_4_counter_1_q1, not_1_out,
       or_1_out, or_2_out;

  m2_4_Counter m2_4_counter_1 (
    .CPu(Adjm), .CPd(1'b0), .CLR(1'b0), .Q1(m2_4_counter_1_q1), .Q0(m2_4_counter_1_q0), .SET(1'b1));  // open: ch
  nor nor_1 (oAdm, m2_4_counter_1_q1, buffer_1_out);
  buf buffer_1 (buffer_1_out, buffer_2_out);
  buf buffer_2 (buffer_2_out, m2_4_counter_1_q0);
  or or_1 (or_1_out, m2_4_counter_1_q0, m2_4_counter_1_q1);
  and and_1 (and_1_out, ~m2_4_counter_1_q1, m2_4_counter_1_q0);  // AND_Gate
  not not_1 (not_1_out, or_1_out);
  and and_2 (and_2_out, and_1_out, or_2_out);
  or or_2 (or_2_out, CPu, CPd);
  T_Flip_Flop t_ff_1 (.clk(and_2_out), .T(1'b1), .Q(am_pm));  // open: Qn, preset, reset, en
  and and_3 (and_3_out, CLR, or_1_out);
  and and_4 (and_4_out, m2_4_counter_1_q0, m2_4_counter_1_q1);
  and and_5 (and_5_out, ~m2_4_counter_1_q0, m2_4_counter_1_q1);  // AND_Gate
  and and_6 (CPu_2, not_1_out, CPu);
  and and_7 (CPd_2, not_1_out, CPd);
  and and_8 (CLR_2, not_1_out, CLR);
  and and_9 (and_9_out, and_4_out, CPu);
  and and_10 (and_10_out, and_4_out, CPd);
  and and_11 (and_11_out, and_4_out, and_3_out);
  and and_12 (and_12_out, and_5_out, and_3_out);
  and and_13 (and_13_out, and_5_out, CPu);
  and and_14 (and_14_out, CPd, and_5_out);
  m60_Counter m60_counter_1 (
    .CLR(and_11_out), .CP(1'b0), .CPu(and_9_out), .Adj(1'b1), .CPd(and_10_out), .Q1(m1), .Q0(m0));  // open: ca, bo
  m12_24_Counter m12_24_counter_1 (
    .CLR(and_12_out), .CP(1'b0), .CPu(and_13_out), .Adj(1'b1), .CPd(and_14_out), .Q1(h1), .Q0(h0), .SET(1'b0));  // open: ch, ca, bo
endmodule

module Main_with_Clock (
  input  CP,
  input  SET,
  input  Adj0,
  input  Adj1,
  input  Adjm,
  input  CPu,
  input  CPd,
  input  CLR,
  output [4:0] Q2,
  output [4:0] Q1,
  output [4:0] Q3,
  output [4:0] Q0,
  output [3:0] h1,
  output [3:0] h0,
  output [3:0] m1,
  output [3:0] m0,
  output [3:0] s1,
  output [3:0] s0,
  output \闹钟 ,
  output \报时 
);

  wire clock_setter_1_am_pm, clock_setter_1_clr_2, clock_setter_1_cpd_2, clock_setter_1_cpu_2,
       clock_setter_1_oadm, main_1_am_pm, multiplexer_1_out, not_1_out, not_2_out;
  wire [3:0] clock_setter_1_h0, clock_setter_1_h1, clock_setter_1_m0, clock_setter_1_m1, main_1_hour0,
       main_1_hour1, main_1_min0, main_1_min1, main_1_sec0, main_1_sec1;

  am_pm am_pm_1 (.Q3(Q3), .Q2(Q2), .Q1(Q1), .Q0(Q0), .AM_PM(multiplexer_1_out), .TT(not_1_out));
  Multiplexer #(.enable("false")) multiplexer_1 (
    .in0(main_1_am_pm), .in1(clock_setter_1_am_pm), .out(multiplexer_1_out), .sel(not_2_out));
  not not_1 (not_1_out, SET);
  not not_2 (not_2_out, clock_setter_1_oadm);
  Multiplexer #(.width(4), .enable("false")) multiplexer_2 (
    .in0(clock_setter_1_h1), .in1(main_1_hour1), .out(h1), .sel(clock_setter_1_oadm));
  Multiplexer #(.width(4), .enable("false")) multiplexer_3 (
    .in0(clock_setter_1_h0), .in1(main_1_hour0), .out(h0), .sel(clock_setter_1_oadm));
  Multiplexer #(.width(4), .enable("false")) multiplexer_4 (
    .in0(clock_setter_1_m1), .in1(main_1_min1), .out(m1), .sel(clock_setter_1_oadm));
  Clock_Setter clock_setter_1 (
    .Adjm(Adjm), .CPu(CPu), .CPd(CPd), .CLR(CLR), .m1(clock_setter_1_m1), .m0(clock_setter_1_m0),
    .CPu_2(clock_setter_1_cpu_2), .CPd_2(clock_setter_1_cpd_2), .CLR_2(clock_setter_1_clr_2),
    .oAdm(clock_setter_1_oadm), .h1(clock_setter_1_h1), .h0(clock_setter_1_h0), .am_pm(clock_setter_1_am_pm));
  Multiplexer #(.width(4), .enable("false")) multiplexer_5 (
    .in0(clock_setter_1_m0), .in1(main_1_min0), .out(m0), .sel(clock_setter_1_oadm));
  Multiplexer #(.width(4), .enable("false")) multiplexer_6 (
    .in1(main_1_sec1), .out(s1), .sel(clock_setter_1_oadm));  // open: in0
  Multiplexer #(.width(4), .enable("false")) multiplexer_7 (
    .in1(main_1_sec0), .out(s0), .sel(clock_setter_1_oadm));  // open: in0
  Main main_1 (
    .CLR(clock_setter_1_clr_2), .Adj0(Adj0), .Adj1(Adj1), .CP(CP), .SET(SET), .CPu(clock_setter_1_cpu_2),
    .CPd(clock_setter_1_cpd_2), .alarm(\报时 ), .sec1(main_1_sec1), .sec0(main_1_sec0), .min1(main_1_min1),
    .min0(main_1_min0), .hour1(main_1_hour1), .hour0(main_1_hour0), .am_pm(main_1_am_pm));
  Clock clock_1 (
    .cam_pm(clock_setter_1_am_pm), .am_pm(main_1_am_pm), .h1(main_1_hour1), .ch1(clock_setter_1_h1),
    .h0(main_1_hour0), .ch0(clock_setter_1_h0), .SET(SET), .s1(main_1_sec1), .m1(main_1_min1),
    .cm1(clock_setter_1_m1), .m0(main_1_min0), .cm0(clock_setter_1_m0), .CP(CP), .alarm(\闹钟 ));
endmodule

// 10unsigned
module test (
  input  in_1,
  input  in_2,
  input  in_3,
  input  in_4,
  input  in_5,
  input  in_6,
  input  in_7,
  input  in_8,
  input  [3:0] in_9,
  input  in_10,
  input  in_11,
  input  in_12,
  input  [3:0] in_13,
  input  [3:0] in_14
);

  wire button_1_out, button_2_out, button_3_out, button_4_out, button_5_out, button_6_out, button_7_out,
       button_8_out, button_9_out, button_10_out, button_11_out, clock_1_out, hour_alarm_1_alarm,
       m12_24_counter_1_bo, m12_24_counter_1_ca, m12_24_counter_1_ch, m60_counter_1_bo,
       \main_with_clock_1_报时 , \main_with_clock_1_闹钟 , n8hz_to_1hz_1__1hz;
  wire [3:0] m12_24_counter_1_q0, m12_24_counter_1_q1, m60_counter_1_q0, m60_counter_1_q1,
       main_with_clock_1_h0, main_with_clock_1_h1, main_with_clock_1_m0, main_with_clock_1_m1,
       main_with_clock_1_s0, main_with_clock_1_s1;
  wire [4:0] am_pm_1_p2, am_pm_1_p3, am_pm_1_p4, am_pm_1_p5, main_with_clock_1_q0, main_with_clock_1_q1,
       main_with_clock_1_q2, main_with_clock_1_q3;

  Clock_part clock_1 (.out(clock_1_out));
  Button button_1 (.out(button_1_out));
  Button button_2 (.out(button_2_out));
  Button button_3 (.out(button_3_out));
  Button button_4 (.out(button_4_out));
  DotMatrix #(.matrixcols(4), .matrixrows(5)) dotmatrix_1 (
    .col0(main_with_clock_1_q3), .col1(main_with_clock_1_q2), .col2(main_with_clock_1_q1),
    .col3(main_with_clock_1_q0));
  Hex_Digit_Display hex_digit_display_1 (.value(main_with_clock_1_h1));  // open: dp
  Hex_Digit_Display hex_digit_display_2 (.value(main_with_clock_1_h0));  // open: dp
  Button button_5 (.out(button_5_out));
  Hex_Digit_Display hex_digit_display_3 (.value(main_with_clock_1_m0));  // open: dp
  Hex_Digit_Display hex_digit_display_4 (.value(main_with_clock_1_m1));  // open: dp
  _8Hz_to_1Hz u_8hz_to_1hz_1 (._8Hz(button_5_out), ._1Hz(n8hz_to_1hz_1__1hz));
  // Probe on n8hz_to_1hz_1__1hz
  Hour_Alarm hour_alarm_1 (.CP(in_7), .alarm(hour_alarm_1_alarm), .sec1(in_9), .min1(in_13), .min0(in_14));
  Hex_Digit_Display hex_digit_display_5 (.value(main_with_clock_1_s0));  // open: dp
  Hex_Digit_Display hex_digit_display_6 (.value(main_with_clock_1_s1));  // open: dp
  LED led_1 (.in(hour_alarm_1_alarm));
  LED led_2 (.in(\main_with_clock_1_闹钟 ));
  Main_with_Clock main_with_clock_1 (
    .CP(clock_1_out), .Adjm(button_1_out), .Adj0(in_3), .CPu(button_2_out), .CPd(button_3_out), .Adj1(in_5),
    .CLR(button_4_out), .SET(in_1), .\闹钟 (\main_with_clock_1_闹钟 ), .\报时 (\main_with_clock_1_报时 ),
    .Q3(main_with_clock_1_q3), .Q2(main_with_clock_1_q2), .Q1(main_with_clock_1_q1),
    .Q0(main_with_clock_1_q0), .h1(main_with_clock_1_h1), .h0(main_with_clock_1_h0),
    .m1(main_with_clock_1_m1), .m0(main_with_clock_1_m0), .s1(main_with_clock_1_s1), .s0(main_with_clock_1_s0));
  LED led_3 (.in(\main_with_clock_1_报时 ));
  DotMatrix #(.matrixcols(4), .matrixrows(5)) dotmatrix_2 (
    .col0(am_pm_1_p2), .col1(am_pm_1_p3), .col2(am_pm_1_p4), .col3(am_pm_1_p5));
  // am_pm am_pm_1: pin names not known; wires that end beside it: in_10, am_pm_1_p2, am_pm_1_p3, am_pm_1_p4, am_pm_1_p5, in_11
  Button button_6 (.out(button_6_out));
  Button button_7 (.out(button_7_out));
  Button button_8 (.out(button_8_out));
  Button button_9 (.out(button_9_out));
  Button button_10 (.out(button_10_out));
  m60_Counter m60_counter_1 (
    .CLR(button_11_out), .CP(in_2), .CPu(button_6_out), .Adj(in_4), .CPd(button_7_out),
    .bo(m60_counter_1_bo), .Q1(m60_counter_1_q1), .Q0(m60_counter_1_q0));  // open: ca
  // Probe on m60_counter_1_q1
  Hex_Digit_Display hex_digit_display_7 (.value(m12_24_counter_1_q1));  // open: dp
  Hex_Digit_Display hex_digit_display_8 (.value(m12_24_counter_1_q0));  // open: dp
  // Probe on m60_counter_1_q0
  // Probe on nothing
  // Probe on m60_counter_1_bo
  Button button_11 (.out(button_11_out));
  // Probe on m12_24_counter_1_ch
  m12_24_Counter m12_24_counter_1 (
    .CLR(button_8_out), .CP(in_6), .CPu(button_9_out), .Adj(in_8), .CPd(button_10_out),
    .ch(m12_24_counter_1_ch), .ca(m12_24_counter_1_ca), .bo(m12_24_counter_1_bo), .Q1(m12_24_counter_1_q1),
    .Q0(m12_24_counter_1_q0), .SET(in_12));
  // Probe on m12_24_counter_1_ca
  // Probe on m12_24_counter_1_bo
endmodule
