// Logisim project 1.circ as structural Verilog: 6 circuits, main circuit sqrX
module sqrX (
  input  [31:0] a,
  input  [31:0] b,
  input  [31:0] c,
  input  [31:0] d,
  output [31:0] a_prime,
  output [31:0] b_prime,
  output [31:0] c_prime,
  output [31:0] d_prime
);

  wire adder_1_cout, adder_2_cout, adder_3_cout;
  wire [31:0] multiplier_1_cout, multiplier_1_out, multiplier_2_cout, multiplier_2_out, multiplier_3_cout,
       multiplier_3_out, multiplier_4_cout, multiplier_4_out, multiplier_5_cout, multiplier_5_out,
       multiplier_6_cout, multiplier_6_out, multiplier_7_out;

  Multiplier #(.width(32)) multiplier_1 (.a(a), .b(a), .out(multiplier_1_out), .cout(multiplier_1_cout));  // open: cin
  Multiplier #(.width(32)) multiplier_2 (
    .a(a), .b(b), .out(multiplier_2_out), .cin(multiplier_1_cout), .cout(multiplier_2_cout));
  Multiplier #(.width(32)) multiplier_3 (
    .a(a), .b(c), .out(multiplier_3_out), .cin(multiplier_2_cout), .cout(multiplier_3_cout));
  Multiplier #(.width(32)) multiplier_4 (
    .a(b), .b(c), .out(multiplier_4_out), .cin(multiplier_3_cout), .cout(multiplier_4_cout));
  Multiplier #(.width(32)) multiplier_5 (
    .a(b), .b(d), .out(multiplier_5_out), .cin(multiplier_4_cout), .cout(multiplier_5_cout));
  Multiplier #(.width(32)) multiplier_6 (
    .a(c), .b(d), .out(multiplier_6_out), .cin(multiplier_5_cout), .cout(multiplier_6_cout));
  Multiplier #(.width(32)) multiplier_7 (.a(d), .b(d), .out(multiplier_7_out), .cin(multiplier_6_cout));  // open: cout
  Adder #(.width(32)) adder_1 (
    .a(multiplier_1_out), .b(multiplier_4_out), .out(a_prime), .cout(adder_1_cout));  // open: cin
  Adder #(.width(32)) adder_2 (
    .a(multiplier_2_out), .b(multiplier_5_out), .out(b_prime), .cin(adder_1_cout), .cout(adder_2_cout));
  Adder #(.width(32)) adder_3 (
    .a(multiplier_3_out), .b(multiplier_6_out), .out(c_prime), .cin(adder_2_cout), .cout(adder_3_cout));
  Adder #(.width(32)) adder_4 (
    .a(multiplier_4_out), .b(multiplier_7_out), .out(d_prime), .cin(adder_3_cout));  // open: cout
endmodule

module sqrX_A (
  input  [31:0] a,
  input  [31:0] b,
  input  [31:0] c,
  input  [31:0] d,
  output [31:0] b_prime_prime,
  output [31:0] a_prime_prime,
  output [31:0] d_prime_prime,
  output [31:0] c_prime_prime
);

  wire [31:0] sqrx_1_a_prime, sqrx_1_c_prime;

  sqrX sqrx_1 (
    .a(a), .b(b), .c(c), .d(d), .a_prime(sqrx_1_a_prime), .b_prime(a_prime_prime), .c_prime(sqrx_1_c_prime),
    .d_prime(c_prime_prime));
  Adder #(.width(32)) adder_1 (.a(sqrx_1_a_prime), .b(a_prime_prime), .out(b_prime_prime));  // open: cin, cout
  Adder #(.width(32)) adder_2 (.a(sqrx_1_c_prime), .b(c_prime_prime), .out(d_prime_prime));  // open: cin, cout
endmodule

module fibo (
  input  start,
  input  clk,
  input  clr,
  input  ni_1,
  output [31:0] Fn
);

  wire and_1_out, register_5_q;
  wire [31:0] a_prime, a_prime_prime, b_prime, b_prime_prime, c_prime, c_prime_prime, d_prime, d_prime_prime,
       multiplexer_1_out, multiplexer_2_out, multiplexer_3_out, multiplexer_4_out, multiplexer_6_out,
       multiplexer_7_out, multiplexer_8_out, multiplexer_9_out, register_1_q, register_2_q, register_3_q,
       register_4_q;

  Multiplexer #(.width(32), .enable("false")) multiplexer_1 (
    .in0({32{1'b0}}), .in1(multiplexer_6_out), .out(multiplexer_1_out), .sel(start));
  Multiplexer #(.width(32), .enable("false")) multiplexer_2 (
    .in0(32'h1), .in1(multiplexer_7_out), .out(multiplexer_2_out), .sel(start));
  Multiplexer #(.width(32), .enable("false")) multiplexer_3 (
    .in0(32'h1), .in1(multiplexer_8_out), .out(multiplexer_3_out), .sel(start));
  Multiplexer #(.width(32), .enable("false")) multiplexer_4 (
    .in0(32'h1), .in1(multiplexer_9_out), .out(multiplexer_4_out), .sel(start));
  Register #(.width(32)) register_1 (.D(multiplexer_1_out), .Q(register_1_q), .clk(clk), .clr(clr));  // open: en
  Register #(.width(32)) register_2 (.D(multiplexer_2_out), .Q(register_2_q), .clk(clk), .clr(clr));  // open: en
  Register #(.width(32)) register_3 (.D(multiplexer_3_out), .Q(register_3_q), .clk(clk), .clr(clr));  // open: en
  Register #(.width(32)) register_4 (.D(multiplexer_4_out), .Q(register_4_q), .clk(clk), .clr(clr));  // open: en
  Register #(.width(1)) register_5 (.D(start), .Q(register_5_q), .clk(clk), .clr(clr));  // open: en
  and and_1 (and_1_out, register_5_q, start);
  Multiplexer #(.width(32), .enable("false")) multiplexer_5 (
    .in0({32{1'b0}}), .in1(register_2_q), .out(Fn), .sel(and_1_out));
  sqrX sqrx_1 (
    .a(register_1_q), .b(register_2_q), .c(register_3_q), .d(register_4_q), .a_prime(a_prime),
    .b_prime(b_prime), .c_prime(c_prime), .d_prime(d_prime));
  sqrX_A sqrx_a_1 (
    .a(register_1_q), .b(register_2_q), .c(register_3_q), .d(register_4_q), .a_prime_prime(a_prime_prime),
    .b_prime_prime(b_prime_prime), .c_prime_prime(c_prime_prime), .d_prime_prime(d_prime_prime));
  Multiplexer #(.width(32), .enable("false")) multiplexer_6 (
    .in0(a_prime), .in1(a_prime_prime), .out(multiplexer_6_out), .sel(ni_1));
  Multiplexer #(.width(32), .enable("false")) multiplexer_7 (
    .in0(b_prime), .in1(b_prime_prime), .out(multiplexer_7_out), .sel(ni_1));
  Multiplexer #(.width(32), .enable("false")) multiplexer_8 (
    .in0(c_prime), .in1(c_prime_prime), .out(multiplexer_8_out), .sel(ni_1));
  Multiplexer #(.width(32), .enable("false")) multiplexer_9 (
    .in0(d_prime), .in1(d_prime_prime), .out(multiplexer_9_out), .sel(ni_1));
endmodule

module bin2dec (
  input  [31:0] Fn,
  output [3:0] D9,
  output [3:0] D8,
  output [3:0] D7,
  output [3:0] D6,
  output [3:0] D5,
  output [3:0] D4,
  output [3:0] D3,
  output [3:0] D2,
  output [3:0] D1,
  output [3:0] D0
);

  wire [31:0] divider_1_out, divider_1_rem, divider_2_out, divider_2_rem, divider_3_out, divider_3_rem,
       divider_4_out, divider_4_rem, divider_5_out, divider_5_rem, divider_6_out, divider_6_rem,
       divider_7_out, divider_7_rem, divider_8_out, divider_8_rem, divider_9_out, divider_9_rem;

  Divider #(.width(32)) divider_1 (.a(Fn), .b(32'ha), .out(divider_1_out), .rem(divider_1_rem));  // open: upper
  Divider #(.width(32)) divider_2 (
    .a(divider_1_out), .b(32'ha), .out(divider_2_out), .rem(divider_2_rem));  // open: upper
  Divider #(.width(32)) divider_3 (
    .a(divider_4_out), .b(32'ha), .out(divider_3_out), .rem(divider_3_rem));  // open: upper
  Divider #(.width(32)) divider_4 (
    .a(divider_2_out), .b(32'ha), .out(divider_4_out), .rem(divider_4_rem));  // open: upper
  Divider #(.width(32)) divider_5 (
    .a(divider_3_out), .b(32'ha), .out(divider_5_out), .rem(divider_5_rem));  // open: upper
  Divider #(.width(32)) divider_6 (
    .a(divider_5_out), .b(32'ha), .out(divider_6_out), .rem(divider_6_rem));  // open: upper
  Divider #(.width(32)) divider_7 (
    .a(divider_6_out), .b(32'ha), .out(divider_7_out), .rem(divider_7_rem));  // open: upper
  Divider #(.width(32)) divider_8 (
    .a(divider_7_out), .b(32'ha), .out(divider_8_out), .rem(divider_8_rem));  // open: upper
  Divider #(.width(32)) divider_9 (
    .a(divider_8_out), .b(32'ha), .out(divider_9_out), .rem(divider_9_rem));  // open: upper
  Bit_Extender #(.in_width(32), .out_width(4)) bit_extender_1 (.in(divider_9_out), .out(D9));
  Bit_Extender #(.in_width(32), .out_width(4)) bit_extender_2 (.in(divider_9_rem), .out(D8));
  Bit_Extender #(.in_width(32), .out_width(4)) bit_extender_3 (.in(divider_8_rem), .out(D7));
  Bit_Extender #(.in_width(32), .out_width(4)) bit_extender_4 (.in(divider_7_rem), .out(D6));
  Bit_Extender #(.in_width(32), .out_width(4)) bit_extender_5 (.in(divider_6_rem), .out(D5));
  Bit_Extender #(.in_width(32), .out_width(4)) bit_extender_6 (.in(divider_5_rem), .out(D4));
  Bit_Extender #(.in_width(32), .out_width(4)) bit_extender_7 (.in(divider_3_rem), .out(D3));
  Bit_Extender #(.in_width(32), .out_width(4)) bit_extender_8 (.in(divider_4_rem), .out(D2));
  Bit_Extender #(.in_width(32), .out_width(4)) bit_extender_9 (.in(divider_2_rem), .out(D1));
  Bit_Extender #(.in_width(32), .out_width(4)) bit_extender_10 (.in(divider_1_rem), .out(D0));
endmodule

module controler (
  input  [5:0] n,
  input  clk,
  input  clr,
  output start,
  output clk_2,
  output clear,
  output ni_1
);

  wire counter_1_carry, d_ff_1_q, d_ff_3_q, multiplexer_1_out, not_1_out, not_2_out, or_1_out,
       shift_register_1_out;

  D_Flip_Flop #(.trigger("falling")) d_ff_1 (
    .clk(clr), .D(1'b1), .Q(d_ff_1_q), .reset(not_1_out));  // open: Qn, preset, en
  not not_1 (not_1_out, clr);
  Counter #(.width(3), .max('h7)) counter_1 (
    .count(not_2_out), .carry(counter_1_carry), .clk(multiplexer_1_out), .clr(clr));  // open: load, D, Q
  Multiplexer #(.enable("false")) multiplexer_1 (.in0(clk), .in1(1'b1), .out(multiplexer_1_out), .sel(d_ff_1_q));
  not not_2 (not_2_out, counter_1_carry);
  and and_1 (clk_2, not_2_out, multiplexer_1_out);
  or or_1 (or_1_out, clr, clk_2);
  Shift_Register #(.length(7)) shift_register_1 (
    .clk(or_1_out), .out(shift_register_1_out), .load(clr), .d0(n[0]), .d1(n[1]), .d2(n[2]), .d3(n[3]),
    .d4(n[4]), .d5(n[5]), .d6(1'b0));  // open: shift, in, clr, q0, q1, q2, q3, q4, q5, q6
  D_Flip_Flop d_ff_2 (.clk(shift_register_1_out), .D(1'b1), .Q(start), .reset(clr));  // open: Qn, preset, en
  D_Flip_Flop d_ff_3 (.clk(multiplexer_1_out), .D(start), .Q(d_ff_3_q), .reset(clr));  // open: Qn, preset, en
  Multiplexer #(.enable("false")) multiplexer_2 (.in1(shift_register_1_out), .out(ni_1), .sel(d_ff_3_q));  // open: in0

  assign clear = clr;
endmodule

module test (
  input  [5:0] n,
  input  [31:0] a,
  input  [31:0] a_2,
  input  [31:0] b,
  input  [31:0] b_2,
  input  [31:0] c,
  input  [31:0] c_2,
  input  [31:0] d,
  input  [31:0] d_2,
  input  start,
  input  [5:0] n_2,
  input  clr,
  input  ni_1,
  input  clk,
  input  [31:0] Fn,
  output [31:0] a_prime,
  output [31:0] a_prime_2,
  output [31:0] b_prime,
  output [31:0] b_prime_2,
  output [31:0] c_prime,
  output [31:0] c_prime_2,
  output [31:0] d_prime,
  output [31:0] d_prime_2,
  output start_2,
  output clr_2,
  output [31:0] Fn_2,
  output ni_1_2,
  output clk_2
);

  wire clk_2_out, clk_out, clr_2_out, clr_out, controler_1_clear, controler_1_clk_2, controler_1_ni_1,
       controler_1_start;
  wire [3:0] bin2dec_1_d0, bin2dec_1_d1, bin2dec_1_d2, bin2dec_1_d3, bin2dec_1_d4, bin2dec_1_d5,
       bin2dec_1_d6, bin2dec_1_d7, bin2dec_1_d8, bin2dec_1_d9, bin2dec_2_d0, bin2dec_2_d1, bin2dec_2_d2,
       bin2dec_2_d3, bin2dec_2_d4, bin2dec_2_d5, bin2dec_2_d6, bin2dec_2_d7, bin2dec_2_d8, bin2dec_2_d9;
  wire [31:0] fibo_1_fn;

  Button u_clr (.out(clr_out));
  Button u_clk (.out(clk_out));
  Button u_clr_2 (.out(clr_2_out));
  Button u_clk_2 (.out(clk_2_out));
  controler controler_1 (
    .clr(clr_out), .ni_1(controler_1_ni_1), .start(controler_1_start), .clk_2(controler_1_clk_2),
    .clear(controler_1_clear), .n(n), .clk(clk_out));
  controler controler_2 (
    .clr(clr_2_out), .ni_1(ni_1_2), .start(start_2), .clk_2(clk_2), .clear(clr_2), .n(n_2), .clk(clk_2_out));
  Hex_Digit_Display hex_digit_display_1 (.value(bin2dec_1_d9));  // open: dp
  Hex_Digit_Display hex_digit_display_2 (.value(bin2dec_1_d8));  // open: dp
  fibo fibo_1 (
    .start(controler_1_start), .clr(controler_1_clear), .ni_1(controler_1_ni_1), .clk(controler_1_clk_2),
    .Fn(fibo_1_fn));
  Hex_Digit_Display hex_digit_display_3 (.value(bin2dec_1_d6));  // open: dp
  Hex_Digit_Display hex_digit_display_4 (.value(bin2dec_1_d7));  // open: dp
  bin2dec bin2dec_1 (
    .Fn(fibo_1_fn), .D1(bin2dec_1_d1), .D2(bin2dec_1_d2), .D3(bin2dec_1_d3), .D4(bin2dec_1_d4),
    .D5(bin2dec_1_d5), .D6(bin2dec_1_d6), .D7(bin2dec_1_d7), .D8(bin2dec_1_d8), .D9(bin2dec_1_d9),
    .D0(bin2dec_1_d0));
  sqrX sqrx_1 (.a(a), .b(b), .c(c), .d(d), .a_prime(a_prime), .b_prime(b_prime), .c_prime(c_prime), .d_prime(d_prime));
  Hex_Digit_Display hex_digit_display_5 (.value(bin2dec_1_d4));  // open: dp
  Hex_Digit_Display hex_digit_display_6 (.value(bin2dec_1_d5));  // open: dp
  fibo fibo_2 (.start(start), .clr(clr), .ni_1(ni_1), .clk(clk), .Fn(Fn_2));
  Hex_Digit_Display hex_digit_display_7 (.value(bin2dec_1_d2));  // open: dp
  Hex_Digit_Display hex_digit_display_8 (.value(bin2dec_1_d3));  // open: dp
  Hex_Digit_Display hex_digit_display_9 (.value(bin2dec_1_d1));  // open: dp
  Hex_Digit_Display hex_digit_display_10 (.value(bin2dec_1_d0));  // open: dp
  Hex_Digit_Display hex_digit_display_11 (.value(bin2dec_2_d8));  // open: dp
  Hex_Digit_Display hex_digit_display_12 (.value(bin2dec_2_d9));  // open: dp
  sqrX_A sqrx_a_1 (
    .a(a_2), .b(b_2), .c(c_2), .d(d_2), .a_prime_prime(a_prime_2), .b_prime_prime(b_prime_2),
    .c_prime_prime(c_prime_2), .d_prime_prime(d_prime_2));
  Hex_Digit_Display hex_digit_display_13 (.value(bin2dec_2_d6));  // open: dp
  Hex_Digit_Display hex_digit_display_14 (.value(bin2dec_2_d7));  // open: dp
  bin2dec bin2dec_2 (
    .Fn(Fn), .D1(bin2dec_2_d1), .D2(bin2dec_2_d2), .D3(bin2dec_2_d3), .D4(bin2dec_2_d4), .D5(bin2dec_2_d5),
    .D6(bin2dec_2_d6), .D7(bin2dec_2_d7), .D8(bin2dec_2_d8), .D9(bin2dec_2_d9), .D0(bin2dec_2_d0));
  Hex_Digit_Display hex_digit_display_15 (.value(bin2dec_2_d5));  // open: dp
  Hex_Digit_Display hex_digit_display_16 (.value(bin2dec_2_d4));  // open: dp
  Hex_Digit_Display hex_digit_display_17 (.value(bin2dec_2_d3));  // open: dp
  Hex_Digit_Display hex_digit_display_18 (.value(bin2dec_2_d2));  // open: dp
  Hex_Digit_Display hex_digit_display_19 (.value(bin2dec_2_d1));  // open: dp
  Hex_Digit_Display hex_digit_display_20 (.value(bin2dec_2_d0));  // open: dp
endmodule
